# Fritzing sketch modelo_circuito (saved by Fritzing 0.9.3b)
breadboards: 1

parts:
  Componente1 = Arduino Uno (Rev3)
  T1 = LM35 Temperature Sensor [package="TO92 [THT]"]
  R1 = Photocell (LDR) [package=THT]
  R2 = Resistor [tolerance=±5% resistance=220 package=THT]
  LED1 = LEDs [package=led10mm]

nets:
  N1: Componente1.A0, T1.Vout
  N2: Componente1.A1, R1.pin_1, R2.Pin_0
  N3: Componente1.D5_PWM, LED1.C
  N4: Componente1.5V, T1.+Vs, R1.pin_0
  GND: Componente1.GND, T1.GND, R2.Pin_1, LED1.A
